// Logisim project 8bit_adder.circ as structural Verilog: 1 circuit, main circuit main
module main (
);

  wire adder_1_cout, adder_1_out, adder_2_cout, adder_2_out, adder_3_cout, adder_3_out, adder_4_cout,
       adder_4_out, adder_5_cout, adder_5_out, adder_6_cout, adder_6_out, adder_7_cout, adder_7_out,
       adder_8_cout, adder_8_out, button_1_out, button_2_out, d_ff_1_q, d_ff_2_q, d_ff_3_q, d_ff_4_q,
       d_ff_5_q, d_ff_6_q, d_ff_7_q, d_ff_8_q, dipswitch_1_p1, dipswitch_1_p2, dipswitch_1_p3,
       dipswitch_1_p4, dipswitch_1_p5, dipswitch_1_p6, dipswitch_1_p7, dipswitch_1_p8;

  // DipSwitch dipswitch_1: pin names not known; wires that end beside it: dipswitch_1_p1, dipswitch_1_p2, dipswitch_1_p3, dipswitch_1_p4, dipswitch_1_p5, dipswitch_1_p6, dipswitch_1_p7, dipswitch_1_p8
  Adder #(.width(1)) adder_1 (.a(d_ff_1_q), .b(dipswitch_1_p1), .out(adder_1_out), .cout(adder_1_cout));  // open: cin
  Adder #(.width(1)) adder_2 (
    .a(d_ff_2_q), .b(dipswitch_1_p2), .out(adder_2_out), .cin(adder_1_cout), .cout(adder_2_cout));
  Adder #(.width(1)) adder_3 (
    .a(d_ff_3_q), .b(dipswitch_1_p3), .out(adder_3_out), .cin(adder_2_cout), .cout(adder_3_cout));
  Adder #(.width(1)) adder_4 (
    .a(d_ff_4_q), .b(dipswitch_1_p4), .out(adder_4_out), .cin(adder_3_cout), .cout(adder_4_cout));
  Adder #(.width(1)) adder_5 (
    .a(d_ff_5_q), .b(dipswitch_1_p5), .out(adder_5_out), .cin(adder_4_cout), .cout(adder_5_cout));
  Adder #(.width(1)) adder_6 (
    .a(d_ff_6_q), .b(dipswitch_1_p6), .out(adder_6_out), .cin(adder_5_cout), .cout(adder_6_cout));
  Adder #(.width(1)) adder_7 (
    .a(d_ff_7_q), .b(dipswitch_1_p7), .out(adder_7_out), .cin(adder_6_cout), .cout(adder_7_cout));
  Adder #(.width(1)) adder_8 (
    .a(d_ff_8_q), .b(dipswitch_1_p8), .out(adder_8_out), .cin(adder_7_cout), .cout(adder_8_cout));
  LED led_1 (.in(adder_8_cout));
  Button button_1 (.out(button_1_out));
  D_Flip_Flop d_ff_1 (.D(adder_1_out), .clk(button_1_out), .Q(d_ff_1_q), .reset(button_2_out));  // open: Qn, preset
  D_Flip_Flop d_ff_2 (.D(adder_2_out), .clk(button_1_out), .Q(d_ff_2_q), .reset(button_2_out));  // open: Qn, preset
  D_Flip_Flop d_ff_3 (.D(adder_3_out), .clk(button_1_out), .Q(d_ff_3_q), .reset(button_2_out));  // open: Qn, preset
  D_Flip_Flop d_ff_4 (.D(adder_4_out), .clk(button_1_out), .Q(d_ff_4_q), .reset(button_2_out));  // open: Qn, preset
  D_Flip_Flop d_ff_5 (.D(adder_5_out), .clk(button_1_out), .Q(d_ff_5_q), .reset(button_2_out));  // open: Qn, preset
  D_Flip_Flop d_ff_6 (.D(adder_6_out), .clk(button_1_out), .Q(d_ff_6_q), .reset(button_2_out));  // open: Qn, preset
  D_Flip_Flop d_ff_7 (.D(adder_7_out), .clk(button_1_out), .Q(d_ff_7_q), .reset(button_2_out));  // open: Qn, preset
  D_Flip_Flop d_ff_8 (.D(adder_8_out), .clk(button_1_out), .Q(d_ff_8_q), .reset(button_2_out));  // open: Qn, preset
  Button button_2 (.out(button_2_out));
  LED led_2 (.in(d_ff_8_q));
  LED led_3 (.in(d_ff_7_q));
  LED led_4 (.in(d_ff_6_q));
  LED led_5 (.in(d_ff_5_q));
  LED led_6 (.in(d_ff_4_q));
  LED led_7 (.in(d_ff_3_q));
  LED led_8 (.in(d_ff_2_q));
  LED led_9 (.in(d_ff_1_q));

  // Notes on the sheet:
  //   Переполнение памяти: 
  //   2^7
  //   2^6
  //   2^5
  //   2^4
  //   2^3
  //   2^1
  //   2^2
  //   2^0
endmodule
