// Logisim project 8bit_adder_subtrator.circ as structural Verilog: 1 circuit, main circuit main
module main (
  input  [7:0] in_1,
  input  [7:0] in_2,
  input  in_3,
  input  in_4,
  input  [7:0] in_5,
  input  [7:0] in_6,
  output [7:0] out_7,
  output [7:0] out_8,
  output [7:0] out_9,
  output [7:0] out_10,
  output [7:0] out_11,
  output [7:0] out_12,
  output [7:0] out_13,
  output [7:0] out_14
);

  wire adder_1_cout, adder_2_cout, adder_3_cout, adder_4_cout, adder_5_cout, adder_6_cout, adder_7_cout,
       adder_8_cout, adder_9_cout, xor_1_out, xor_2_out, xor_3_out, xor_4_out, xor_5_out, xor_6_out,
       xor_7_out, xor_8_out;
  wire [7:0] controlled_inverter_1_out;

  xor xor_1 (xor_1_out, in_4, in_5[0]);
  xor xor_2 (xor_2_out, in_4, in_5[1]);
  xor xor_3 (xor_3_out, in_4, in_5[2]);
  xor xor_4 (xor_4_out, in_4, in_5[3]);
  xor xor_5 (xor_5_out, in_4, in_5[4]);
  xor xor_6 (xor_6_out, in_4, in_5[5]);
  xor xor_7 (xor_7_out, in_4, in_5[6]);
  xor xor_8 (xor_8_out, in_4, in_5[7]);
  assign controlled_inverter_1_out = in_3 ? ~in_1 : 8'bz;  // Controlled_Inverter controlled_inverter_1
  Adder adder_1 (.a(controlled_inverter_1_out), .b(in_2), .out(out_8), .cin(in_3), .cout(adder_1_cout));
  LED led_1 (.in(adder_1_cout));
  Adder #(.width(1)) adder_2 (.a(xor_1_out), .b(in_6[0]), .out(out_13[0]), .cin(in_4), .cout(adder_2_cout));
  Adder #(.width(1)) adder_3 (.a(xor_2_out), .b(in_6[1]), .out(out_13[1]), .cin(adder_2_cout), .cout(adder_3_cout));
  Adder #(.width(1)) adder_4 (.a(xor_3_out), .b(in_6[2]), .out(out_13[2]), .cin(adder_3_cout), .cout(adder_4_cout));
  Adder #(.width(1)) adder_5 (.a(xor_4_out), .b(in_6[3]), .out(out_13[3]), .cin(adder_4_cout), .cout(adder_5_cout));
  Adder #(.width(1)) adder_6 (.a(xor_5_out), .b(in_6[4]), .out(out_13[4]), .cin(adder_5_cout), .cout(adder_6_cout));
  Adder #(.width(1)) adder_7 (.a(xor_6_out), .b(in_6[5]), .out(out_13[5]), .cin(adder_6_cout), .cout(adder_7_cout));
  Adder #(.width(1)) adder_8 (.a(xor_7_out), .b(in_6[6]), .out(out_13[6]), .cin(adder_7_cout), .cout(adder_8_cout));
  Adder #(.width(1)) adder_9 (.a(xor_8_out), .b(in_6[7]), .out(out_13[7]), .cin(adder_8_cout), .cout(adder_9_cout));
  LED led_2 (.in(adder_9_cout));

  assign out_7 = in_1;
  assign out_9 = out_8;
  assign out_10 = in_2;
  assign out_11 = in_5;
  assign out_12 = in_6;
  assign out_14 = out_13;
endmodule
