// Logisim project Harvard_Arch.circ as structural Verilog: 1 circuit, main circuit main
module main (
  input  in_1,
  input  in_2,
  input  in_3,
  input  in_4,
  input  in_5,
  output [15:0] out_6,
  output [15:0] out_7,
  output [7:0] out_8,
  output [7:0] out_9,
  output [15:0] out_10,
  output [7:0] out_11,
  output [7:0] out_12,
  output [7:0] out_13,
  output [7:0] out_14,
  output [15:0] out_15,
  output [15:0] out_16,
  output [7:0] out_17,
  output [7:0] out_18,
  output [15:0] out_19,
  output [7:0] out_20,
  output [7:0] out_21,
  output [7:0] out_22,
  output [7:0] out_23
);

  wire adder_1_cout, adder_2_cout, adder_3_cout, adder_4_cout, adder_5_cout, adder_6_cout, adder_7_cout,
       adder_8_cout, button_1_out, button_2_out, clock_1_out, clock_2_out, multiplexer_1_out,
       multiplexer_3_out, multiplexer_5_out, multiplexer_6_out, multiplexer_8_out, multiplexer_9_out;
  wire [7:0] adder_8_out, bitselector_1_out, d_ff_8_q, multiplexer_7_out, xor_8_out;
  wire [15:0] counter_1_q, multiplexer_2_out, multiplexer_4_out;

  Clock clock_1 (.out(clock_1_out));
  Counter #(.max('hffff), .width(16)) counter_1 (
    .Q(counter_1_q), .clk(clock_1_out), .clr(multiplexer_1_out));  // open: load, D, count, carry, up
  Multiplexer multiplexer_1 (.in0(out_12[7]), .in1(in_3), .out(multiplexer_1_out), .sel(in_3));
  Multiplexer #(.width(16)) multiplexer_2 (.in0(counter_1_q), .in1(out_6), .out(multiplexer_2_out), .sel(in_1));
  Multiplexer multiplexer_3 (.in0(clock_1_out), .in1(in_2), .out(multiplexer_3_out), .sel(in_1));
  Multiplexer #(.width(16)) multiplexer_4 (.in0(counter_1_q), .in1(out_15), .out(multiplexer_4_out), .sel(in_4));
  Multiplexer multiplexer_5 (.in0(clock_1_out), .in1(in_5), .out(multiplexer_5_out), .sel(in_4));
  Multiplexer multiplexer_6 (.in0(multiplexer_8_out), .in1(button_2_out), .out(multiplexer_6_out), .sel(in_4));
  DipSwitch #(.number(16)) dipswitch_1 (
    .sw1(out_6[15]), .sw2(out_6[14]), .sw3(out_6[13]), .sw4(out_6[12]), .sw5(out_6[11]), .sw6(out_6[10]),
    .sw7(out_6[9]), .sw8(out_6[8]), .sw9(out_6[7]), .sw10(out_6[6]), .sw11(out_6[5]), .sw12(out_6[4]),
    .sw13(out_6[3]), .sw14(out_6[2]), .sw15(out_6[1]), .sw16(out_6[0]));
  RAM #(.addrWidth(16), .asyncread("true")) ram_1 (
    .addr(multiplexer_2_out), .we(button_1_out), .oe(multiplexer_3_out), .clk(button_1_out), .din(out_8),
    .dout(out_12));
  DipSwitch #(.number(16)) dipswitch_2 (
    .sw1(out_15[15]), .sw2(out_15[14]), .sw3(out_15[13]), .sw4(out_15[12]), .sw5(out_15[11]),
    .sw6(out_15[10]), .sw7(out_15[9]), .sw8(out_15[8]), .sw9(out_15[7]), .sw10(out_15[6]), .sw11(out_15[5]),
    .sw12(out_15[4]), .sw13(out_15[3]), .sw14(out_15[2]), .sw15(out_15[1]), .sw16(out_15[0]));
  RAM #(.addrWidth(16), .asyncread("true")) ram_2 (
    .addr(multiplexer_4_out), .we(multiplexer_6_out), .oe(multiplexer_5_out), .clk(multiplexer_6_out),
    .din(multiplexer_7_out), .dout(out_21));
  Multiplexer #(.width(8)) multiplexer_7 (.in0(d_ff_8_q), .in1(out_17), .out(multiplexer_7_out), .sel(in_4));
  Multiplexer multiplexer_8 (.in0(out_12[0]), .in1(button_2_out), .out(multiplexer_8_out), .sel(in_4));
  DipSwitch dipswitch_3 (
    .sw1(out_8[7]), .sw2(out_8[6]), .sw3(out_8[5]), .sw4(out_8[4]), .sw5(out_8[3]), .sw6(out_8[2]),
    .sw7(out_8[1]), .sw8(out_8[0]));
  Button button_1 (.out(button_1_out));
  DipSwitch dipswitch_4 (
    .sw1(out_17[7]), .sw2(out_17[6]), .sw3(out_17[5]), .sw4(out_17[4]), .sw5(out_17[3]), .sw6(out_17[2]),
    .sw7(out_17[1]), .sw8(out_17[0]));
  Button button_2 (.out(button_2_out));
  Clock clock_2 (.out(clock_2_out));
  Multiplexer #(.enable("true")) multiplexer_9 (
    .in0(out_12[4]), .in1(out_12[5]), .out(multiplexer_9_out), .sel(out_12[5]), .en(clock_2_out));
  xor xor_1 (xor_8_out[7], out_21[7], out_12[1]);
  xor xor_2 (xor_8_out[6], out_21[6], out_12[1]);
  xor xor_3 (xor_8_out[5], out_21[5], out_12[1]);
  Adder #(.width(1)) adder_1 (
    .a(d_ff_8_q[7]), .b(xor_8_out[7]), .out(adder_8_out[7]), .cin(adder_2_cout), .cout(adder_1_cout));
  LED led_1 (.in(adder_1_cout));
  BitSelector #(.group(8), .width(16)) bitselector_1 (
    .in({adder_8_out, out_21}), .out(bitselector_1_out), .sel(out_12[4]));
  D_Flip_Flop d_ff_1 (
    .D(bitselector_1_out[7]), .clk(multiplexer_9_out), .Q(d_ff_8_q[7]), .reset(out_12[7]));  // open: Qn, preset
  xor xor_4 (xor_8_out[4], out_21[4], out_12[1]);
  xor xor_5 (xor_8_out[3], out_21[3], out_12[1]);
  xor xor_6 (xor_8_out[2], out_21[2], out_12[1]);
  Adder #(.width(1)) adder_2 (
    .a(d_ff_8_q[6]), .b(xor_8_out[6]), .out(adder_8_out[6]), .cin(adder_3_cout), .cout(adder_2_cout));
  D_Flip_Flop d_ff_2 (
    .D(bitselector_1_out[6]), .clk(multiplexer_9_out), .Q(d_ff_8_q[6]), .reset(out_12[7]));  // open: Qn, preset
  xor xor_7 (xor_8_out[1], out_21[1], out_12[1]);
  xor xor_8 (xor_8_out[0], out_21[0], out_12[1]);
  D_Flip_Flop d_ff_3 (
    .D(bitselector_1_out[5]), .clk(multiplexer_9_out), .Q(d_ff_8_q[5]), .reset(out_12[7]));  // open: Qn, preset
  Adder #(.width(1)) adder_3 (
    .a(d_ff_8_q[5]), .b(xor_8_out[5]), .out(adder_8_out[5]), .cin(adder_4_cout), .cout(adder_3_cout));
  D_Flip_Flop d_ff_4 (
    .D(bitselector_1_out[4]), .clk(multiplexer_9_out), .Q(d_ff_8_q[4]), .reset(out_12[7]));  // open: Qn, preset
  Adder #(.width(1)) adder_4 (
    .a(d_ff_8_q[4]), .b(xor_8_out[4]), .out(adder_8_out[4]), .cin(adder_5_cout), .cout(adder_4_cout));
  D_Flip_Flop d_ff_5 (
    .D(bitselector_1_out[3]), .clk(multiplexer_9_out), .Q(d_ff_8_q[3]), .reset(out_12[7]));  // open: Qn, preset
  Adder #(.width(1)) adder_5 (
    .a(d_ff_8_q[3]), .b(xor_8_out[3]), .out(adder_8_out[3]), .cin(adder_6_cout), .cout(adder_5_cout));
  D_Flip_Flop d_ff_6 (
    .D(bitselector_1_out[2]), .clk(multiplexer_9_out), .Q(d_ff_8_q[2]), .reset(out_12[7]));  // open: Qn, preset
  Adder #(.width(1)) adder_6 (
    .a(d_ff_8_q[2]), .b(xor_8_out[2]), .out(adder_8_out[2]), .cin(adder_7_cout), .cout(adder_6_cout));
  Adder #(.width(1)) adder_7 (
    .a(d_ff_8_q[1]), .b(xor_8_out[1]), .out(adder_8_out[1]), .cin(adder_8_cout), .cout(adder_7_cout));
  D_Flip_Flop d_ff_7 (
    .D(bitselector_1_out[1]), .clk(multiplexer_9_out), .Q(d_ff_8_q[1]), .reset(out_12[7]));  // open: Qn, preset
  Adder #(.width(1)) adder_8 (
    .a(d_ff_8_q[0]), .b(xor_8_out[0]), .out(adder_8_out[0]), .cin(out_12[1]), .cout(adder_8_cout));
  D_Flip_Flop d_ff_8 (
    .D(bitselector_1_out[0]), .clk(multiplexer_9_out), .Q(d_ff_8_q[0]), .reset(out_12[7]));  // open: Qn, preset

  assign out_7 = out_6;
  assign out_9 = out_8;
  assign out_10 = out_6;
  assign out_11 = out_8;
  assign out_13 = out_12;
  assign out_14 = out_12;
  assign out_16 = out_15;
  assign out_18 = out_17;
  assign out_19 = out_15;
  assign out_20 = out_17;
  assign out_22 = out_21;
  assign out_23 = out_21;

  // Notes on the sheet:
  //   |Операция   Код| Загрузить  10h| Сохранить  11h| Сложить    20h| Вычесть    22h| Остановить FFh|
endmodule
